// Logisim project 1803175(Lab-04).circ as structural Verilog: 3 circuits, main circuit 4.1.1(Drag And drop)
module _4_1_1_Drag_And_drop (
  input  a,
  input  b,
  input  c,
  input  d,
  output out_5
);

  wire and_1_out, and_2_out, and_3_out, and_4_out, and_5_out, and_6_out, and_7_out, and_8_out, not_1_out,
       not_2_out, not_3_out, not_4_out;

  not not_1 (not_1_out, a);
  not not_2 (not_2_out, b);
  not not_3 (not_3_out, c);
  not not_4 (not_4_out, d);
  and and_1 (and_1_out, not_1_out, not_2_out, not_3_out, not_4_out);
  and and_2 (and_2_out, not_1_out, not_2_out, c, not_4_out);
  and and_3 (and_3_out, not_1_out, not_2_out, c, d);
  and and_4 (and_4_out, not_1_out, b, not_3_out, not_4_out);
  or or_1 (out_5, and_1_out, and_2_out, and_3_out, and_4_out, and_5_out, and_6_out, and_7_out, and_8_out);
  and and_5 (and_5_out, a, b, not_3_out, not_4_out);
  and and_6 (and_6_out, a, not_2_out, c, not_4_out);
  and and_7 (and_7_out, a, b, c, not_4_out);
  and and_8 (and_8_out, a, b, c, d);

  // Notes on the sheet:
  //   MSB
  //   LSB
  //   m0
  //   m2
  //   m3
  //   4.1.1: Implementation of Verious Logic Function (For example: F(a,b,c,d) = SOP(0,2,3,4,6,10,14,15)) using Drag and drop.
  //   m4
  //   m6
  //   m10
  //   m14
  //   m15
endmodule

module _4_1_2_Circuit_Analysis (
  input  a,
  input  b,
  input  c,
  input  d,
  output X
);

  wire and_1_out, and_2_out, and_3_out, and_4_out, not_1_out, not_2_out, not_3_out, not_4_out, not_5_out;

  not not_1 (not_1_out, a);
  and and_1 (and_1_out, not_1_out, not_2_out);
  not not_2 (not_2_out, d);
  not not_3 (not_3_out, a);
  not not_4 (not_4_out, b);
  and and_2 (and_2_out, not_3_out, not_4_out, c);
  and and_3 (and_3_out, c, not_5_out);
  not not_5 (not_5_out, d);
  and and_4 (and_4_out, a, b, c);
  or or_1 (X, and_1_out, and_2_out, and_3_out, and_4_out);

  // Notes on the sheet:
  //   MSB
  //   LSB
  //   4.1.2 Implementation of Verious Logic Function (For example: F(a,b,c,d)= SOP(0,2,3,4,6,10,14,15) ) Using Circuit Analysis
endmodule

module _4_2_1 (
  input  a,
  input  b,
  input  c,
  input  d,
  output X
);

  wire and_1_out, and_2_out, and_3_out, and_4_out, not_1_out, not_2_out, not_3_out, not_4_out, not_5_out;

  not not_1 (not_1_out, a);
  and and_1 (and_1_out, not_1_out, not_2_out);
  not not_2 (not_2_out, d);
  not not_3 (not_3_out, a);
  and and_2 (and_2_out, not_3_out, not_4_out, c);
  not not_4 (not_4_out, b);
  and and_3 (and_3_out, c, not_5_out);
  not not_5 (not_5_out, d);
  and and_4 (and_4_out, a, b, c);
  or or_1 (X, and_1_out, and_2_out, and_3_out, and_4_out);

  // Notes on the sheet:
  //   MSB
  //   LSB
  //   4.2.1: Verifying the result of the simplefied version of the F in 4.1 
endmodule
