// Logisim project 1803175(Lab-05).circ as structural Verilog: 5 circuits, main circuit 5.1.1
module _5_1_1 (
  input  x,
  input  y,
  output s,
  output c
);

  wire and_1_out, and_2_out, not_1_out, not_2_out;

  not not_1 (not_1_out, x);
  not not_2 (not_2_out, y);
  and and_1 (and_1_out, x, not_2_out);
  and and_2 (and_2_out, not_1_out, y);
  or or_1 (s, and_1_out, and_2_out);
  and and_3 (c, x, y);

  // Notes on the sheet:
  //   5.1.1Verifyinng the Half Adder Circuit(using the basic gates) 
endmodule

module _5_1_2 (
  input  x,
  input  y,
  output s,
  output c
);

  xor xor_1 (s, x, y);
  and and_1 (c, x, y);

  // Notes on the sheet:
  //   5.1.2 Verifying the HAlf Adder Circuit(using the universal gate) 
endmodule

module _5_2_1 (
  input  x,
  input  y,
  input  z,
  output s,
  output c
);

  wire and_1_out, and_2_out, and_3_out, and_4_out, and_5_out, and_6_out, and_7_out, not_1_out, not_2_out,
       not_3_out;

  not not_1 (not_1_out, x);
  not not_2 (not_2_out, y);
  not not_3 (not_3_out, z);
  and and_1 (and_1_out, not_1_out, not_2_out, z);
  and and_2 (and_2_out, not_1_out, y, not_3_out);
  and and_3 (and_3_out, x, not_2_out, not_3_out);
  and and_4 (and_4_out, x, y, z);
  and and_5 (and_5_out, x, y);
  and and_6 (and_6_out, y, z);
  and and_7 (and_7_out, z, x);
  or or_1 (s, and_1_out, and_2_out, and_3_out, and_4_out);
  or or_2 (c, and_5_out, and_6_out, and_7_out);

  // Notes on the sheet:
  //   5.2.1 Full adder (Using the basic gates)
endmodule

module _5_2_2 (
  input  x,
  input  y,
  input  z,
  output s,
  output c
);

  wire and_1_out, and_2_out, and_3_out, xor_1_out;

  xor xor_1 (xor_1_out, x, y);
  and and_1 (and_1_out, x, y);
  and and_2 (and_2_out, y, z);
  and and_3 (and_3_out, z, x);
  xor xor_2 (s, xor_1_out, z);
  or or_1 (c, and_1_out, and_2_out, and_3_out);

  // Notes on the sheet:
  //   5.2.2 Full adder (Using the universal gates)
endmodule

module _5_3 (
  input  x,
  input  y,
  input  z,
  output s,
  output c
);

  wire and_1_out, and_2_out, xor_1_out;

  xor xor_1 (xor_1_out, x, y);
  and and_1 (and_1_out, x, y);
  xor xor_2 (s, xor_1_out, z);
  and and_2 (and_2_out, xor_1_out, z);
  or or_1 (c, and_2_out, and_1_out);

  // Notes on the sheet:
  //   5.3 Implementing the Full Adder Circuit using the Half adder and verifying the result
endmodule
