// Logisim project 1803175(Lab-06).circ as structural Verilog: 2 circuits, main circuit 6.1
module _6_1 (
  input  x,
  input  y,
  input  z,
  output out_4
);

  wire and_1_out, and_2_out, and_3_out, and_4_out, and_5_out, not_1_out, not_2_out, not_3_out, or_1_out;

  not not_1 (not_1_out, x);
  not not_2 (not_2_out, y);
  not not_3 (not_3_out, z);
  or or_1 (or_1_out, z, not_3_out);
  and and_1 (and_1_out, z, not_3_out);
  and and_2 (and_2_out, not_1_out, not_2_out, z);
  and and_3 (and_3_out, not_1_out, y, not_3_out);
  and and_4 (and_4_out, x, not_2_out, and_1_out);
  and and_5 (and_5_out, or_1_out, x, y);
  or or_2 (out_4, and_2_out, and_3_out, and_4_out, and_5_out);

  // Notes on the sheet:
  //   6.1: Verifying various multiplexers input and output
  //   f(x,y,z)=sop(1,2,6,7)
endmodule

module _6_2 (
  input  D3,
  input  D2,
  input  D1,
  input  D0,
  output y,
  output x,
  output v
);

  wire and_1_out, not_1_out;

  or or_1 (x, D3, D2);
  not not_1 (not_1_out, D2);
  and and_1 (and_1_out, not_1_out, D1);
  or or_2 (y, D3, and_1_out);
  or or_3 (v, x, D1, D0);

  // Notes on the sheet:
  //   6.1: Verifying various Encoders input and output 
endmodule
