// Logisim project 1803175(Lab-09).circ as structural Verilog: 3 circuits, main circuit 9.1
module _9_1 (
  input  INPUT,
  input  ENABLE,
  output MSB,
  output out_4,
  output LSB
);

  wire clock_1_out, j_k_ff_1_q, j_k_ff_2_q;

  Clock clock_1 (.out(clock_1_out));
  J_K_Flip_Flop j_k_ff_1 (
    .J(INPUT), .clk(clock_1_out), .K(INPUT), .Q(j_k_ff_1_q), .Qn(LSB), .en(ENABLE));  // open: preset, reset
  J_K_Flip_Flop j_k_ff_2 (
    .J(INPUT), .clk(j_k_ff_1_q), .K(INPUT), .Q(j_k_ff_2_q), .Qn(out_4), .en(ENABLE));  // open: preset, reset
  J_K_Flip_Flop j_k_ff_3 (.J(INPUT), .clk(j_k_ff_2_q), .K(INPUT), .Qn(MSB), .en(ENABLE));  // open: Q, preset, reset

  // Notes on the sheet:
  //   CLK
  //   LSB
  //   9.1: Desigening a 3 bit asyncronous counter using JK FF(Up) 
  //   MSB
endmodule

module _9_2_1 (
  input  INPUT,
  input  EMABLE,
  output out_3,
  output out_4,
  output LSB
);

  wire and_1_out, clock_1_out;

  Clock clock_1 (.out(clock_1_out));
  J_K_Flip_Flop j_k_ff_1 (.J(INPUT), .clk(clock_1_out), .K(INPUT), .Q(LSB), .en(EMABLE));  // open: Qn, preset, reset
  J_K_Flip_Flop j_k_ff_2 (.J(LSB), .clk(clock_1_out), .K(LSB), .Q(out_4), .en(EMABLE));  // open: Qn, preset, reset
  and and_1 (and_1_out, LSB, out_4);
  J_K_Flip_Flop j_k_ff_3 (
    .J(and_1_out), .clk(clock_1_out), .K(and_1_out), .Q(out_3), .en(EMABLE));  // open: Qn, preset, reset

  // Notes on the sheet:
  //   CLK
  //   LSB
  //   A
  //   MSB
  //   9.2.1: Desigening a 3 bit syncronous counter using JK FF(Up) 
  //   B
  //   MSB
  //   C
endmodule

module _9_2_2 (
  input  INPUT,
  input  ENABLE,
  output out_3,
  output out_4,
  output LSB
);

  wire and_1_out, and_2_out, and_3_out, clock_1_out, j_k_ff_1_qn, not_1_out, or_1_out, t_ff_1_qn;

  Clock clock_1 (.out(clock_1_out));
  J_K_Flip_Flop j_k_ff_1 (
    .J(INPUT), .clk(clock_1_out), .K(INPUT), .Q(LSB), .Qn(j_k_ff_1_qn), .en(ENABLE));  // open: preset, reset
  T_Flip_Flop t_ff_1 (.clk(clock_1_out), .T(LSB), .Q(out_4), .Qn(t_ff_1_qn), .en(ENABLE));  // open: preset, reset
  and and_1 (and_1_out, out_3, t_ff_1_qn);
  not not_1 (not_1_out, out_3);
  and and_2 (and_2_out, not_1_out, out_4, LSB);
  and and_3 (and_3_out, out_4, j_k_ff_1_qn, out_3);
  D_Flip_Flop d_ff_1 (.clk(clock_1_out), .D(or_1_out), .Q(out_3), .en(ENABLE));  // open: Qn, preset, reset
  or or_1 (or_1_out, and_1_out, and_2_out, and_3_out);

  // Notes on the sheet:
  //   CLK
  //   MSB
  //   LSB
  //   A
  //   9.2.2: Desigening a 3 bit syncronous counter using JK, T and D FF(Up) 
  //   B
  //   MSB
  //   C
endmodule
