// Logisim project 1803175(Lab-2).circ as structural Verilog: 3 circuits, main circuit 2.1
module _2_1 (
  input  in_1
);

  wire not_1_out;

  not not_1 (not_1_out, in_1);
  LED led_1 (.in(not_1_out));

  // Notes on the sheet:
  //   NOT Gate
endmodule

module _2_2 (
  input  in_1,
  input  in_2,
  input  in_3,
  input  in_4,
  input  in_5
);

  wire and_1_out;

  and and_1 (and_1_out, in_1, in_2, in_3, in_4, in_5);
  LED led_1 (.in(and_1_out));

  // Notes on the sheet:
  //   AND Gate
endmodule

module _2_3 (
  input  in_1,
  input  in_2,
  input  in_3,
  input  in_4,
  input  in_5
);

  wire or_1_out;

  or or_1 (or_1_out, in_1, in_2, in_3, in_4, in_5);
  LED led_1 (.in(or_1_out));

  // Notes on the sheet:
  //   OR Gate
endmodule
