// Logisim project 1803175(Lab-3).circ as structural Verilog: 8 circuits, main circuit 3.1.1
module _3_1_1 (
  input  in_1,
  input  in_2,
  input  in_3,
  input  in_4,
  input  in_5,
  output out_6
);

  nor nor_1 (out_6, in_1, in_2, in_3, in_4, in_5);

  // Notes on the sheet:
  //   3.1.1: Verifying the Basic NOR gate (upto 5 inputs) for all inp[ut combinations (using Drag and Drop)
endmodule

module _3_1_2 (
  input  a,
  input  b,
  input  c,
  input  d,
  input  e,
  output x
);

  wire not_1_out, not_2_out, not_3_out, not_4_out, not_5_out;

  not not_1 (not_1_out, a);
  not not_2 (not_2_out, b);
  not not_3 (not_3_out, c);
  not not_4 (not_4_out, d);
  not not_5 (not_5_out, e);
  and and_1 (x, not_1_out, not_2_out, not_3_out, not_4_out, not_5_out);

  // Notes on the sheet:
  //   3.1.2: Verifying the basic NOR gate (upto 5 inputs) for all input combinations. (using Citcuit Analyze)
endmodule

module _3_2_1 (
  input  in_1,
  input  in_2,
  input  in_3,
  input  in_4,
  input  in_5,
  output out_6
);

  nand nand_1 (out_6, in_1, in_2, in_3, in_4, in_5);

  // Notes on the sheet:
  //   3.2.1: Verifying the basic NAND gate (upto 5 inputs) for all input combinations(Using Drag and Drop)
endmodule

module _3_2_2 (
  input  a,
  input  b,
  input  c,
  input  d,
  input  e,
  output x
);

  wire not_1_out, not_2_out, not_3_out, not_4_out, not_5_out;

  not not_1 (not_1_out, a);
  not not_2 (not_2_out, b);
  not not_3 (not_3_out, c);
  not not_4 (not_4_out, d);
  not not_5 (not_5_out, e);
  or or_1 (x, not_1_out, not_2_out, not_3_out, not_4_out, not_5_out);

  // Notes on the sheet:
  //   3.2,2: verifying the basic NAND gate (upto 5 inputs) for all input combinations(using Circuit Analyze)
endmodule

module _3_3_1 (
  input  in_1,
  input  in_2,
  input  in_3,
  input  in_4,
  input  in_5,
  output out_6
);

  xor xor_1 (out_6, in_1, in_2, in_3, in_4, in_5);

  // Notes on the sheet:
  //   3.3.1: Verifying the basic XOR gate (upto 5 inputs) for all input combinations (using Drag and Drop)
endmodule

module _3_3_2 (
  input  a,
  input  b,
  input  c,
  input  d,
  input  e,
  output x
);

  wire and_1_out, and_2_out, and_3_out, and_4_out, and_5_out, and_6_out, and_7_out, and_8_out, and_9_out,
       and_10_out, and_11_out, and_12_out, and_13_out, and_14_out, and_15_out, and_16_out, not_1_out,
       not_2_out, not_3_out, not_4_out, not_5_out, not_6_out, not_7_out, not_8_out, not_9_out, not_10_out,
       not_11_out, not_12_out, not_13_out, not_14_out, not_15_out, not_16_out, not_17_out, not_18_out,
       not_19_out, not_20_out, not_21_out, not_22_out, not_23_out, not_24_out, not_25_out, not_26_out,
       not_27_out, not_28_out, not_29_out, not_30_out, not_31_out, not_32_out, not_33_out, not_34_out,
       not_35_out, not_36_out, not_37_out, not_38_out, not_39_out, not_40_out;

  not not_1 (not_1_out, a);
  not not_2 (not_2_out, b);
  not not_3 (not_3_out, c);
  not not_4 (not_4_out, d);
  not not_5 (not_5_out, a);
  not not_6 (not_6_out, b);
  not not_7 (not_7_out, c);
  not not_8 (not_8_out, e);
  not not_9 (not_9_out, a);
  not not_10 (not_10_out, b);
  not not_11 (not_11_out, d);
  not not_12 (not_12_out, e);
  not not_13 (not_13_out, a);
  not not_14 (not_14_out, b);
  not not_15 (not_15_out, a);
  not not_16 (not_16_out, c);
  not not_17 (not_17_out, d);
  not not_18 (not_18_out, e);
  not not_19 (not_19_out, a);
  not not_20 (not_20_out, c);
  not not_21 (not_21_out, a);
  not not_22 (not_22_out, d);
  not not_23 (not_23_out, a);
  not not_24 (not_24_out, e);
  not not_25 (not_25_out, b);
  not not_26 (not_26_out, c);
  not not_27 (not_27_out, d);
  not not_28 (not_28_out, e);
  not not_29 (not_29_out, b);
  not not_30 (not_30_out, c);
  not not_31 (not_31_out, b);
  not not_32 (not_32_out, d);
  not not_33 (not_33_out, b);
  not not_34 (not_34_out, e);
  not not_35 (not_35_out, c);
  not not_36 (not_36_out, d);
  not not_37 (not_37_out, c);
  not not_38 (not_38_out, e);
  not not_39 (not_39_out, d);
  not not_40 (not_40_out, e);
  and and_1 (and_1_out, not_1_out, not_2_out, not_3_out, not_4_out, e);
  and and_2 (and_2_out, not_5_out, not_6_out, not_7_out, d, not_8_out);
  and and_3 (and_3_out, not_9_out, not_10_out, c, not_11_out, not_12_out);
  and and_4 (and_4_out, not_13_out, not_14_out, c, d, e);
  and and_5 (and_5_out, not_15_out, b, not_16_out, not_17_out, not_18_out);
  and and_6 (and_6_out, not_19_out, b, not_20_out, d, e);
  and and_7 (and_7_out, not_21_out, b, c, not_22_out, e);
  and and_8 (and_8_out, not_23_out, b, c, d, not_24_out);
  and and_9 (and_9_out, a, not_25_out, not_26_out, not_27_out, not_28_out);
  and and_10 (and_10_out, a, not_29_out, not_30_out, d, e);
  and and_11 (and_11_out, a, not_31_out, c, not_32_out, e);
  and and_12 (and_12_out, a, not_33_out, c, d, not_34_out);
  and and_13 (and_13_out, a, b, not_35_out, not_36_out, e);
  and and_14 (and_14_out, a, b, not_37_out, d, not_38_out);
  and and_15 (and_15_out, a, b, c, not_39_out, not_40_out);
  and and_16 (and_16_out, a, b, c, d, e);
  or or_1 (x, and_1_out, and_2_out, and_3_out, and_4_out, and_5_out, and_6_out, and_7_out, and_8_out, and_9_out, and_10_out, and_11_out, and_12_out, and_13_out, and_14_out, and_15_out, and_16_out);

  // Notes on the sheet:
  //   3.3.2: Verifying the basic XOR gate(upto 5 inputs) for all input combinations(using circuit analysis)
endmodule

module _3_4_1 (
  input  in_1,
  input  in_2,
  input  in_3,
  input  in_4,
  input  in_5,
  output out_6
);

  xnor xnor_1 (out_6, in_1, in_2, in_3, in_4, in_5);

  // Notes on the sheet:
  //   3.4.1: Verifying the basic XNOR gate(upto 5 inputs) for all input combinations (using Drag and Crop)
endmodule

module _3_4_2 (
  input  a,
  input  b,
  input  c,
  input  d,
  input  e,
  output x
);

  wire and_1_out, and_2_out, and_3_out, and_4_out, and_5_out, and_6_out, and_7_out, and_8_out, and_9_out,
       and_10_out, and_11_out, and_12_out, and_13_out, and_14_out, and_15_out, and_16_out, not_1_out,
       not_2_out, not_3_out, not_4_out, not_5_out, not_6_out, not_7_out, not_8_out, not_9_out, not_10_out,
       not_11_out, not_12_out, not_13_out, not_14_out, not_15_out, not_16_out, not_17_out, not_18_out,
       not_19_out, not_20_out, not_21_out, not_22_out, not_23_out, not_24_out, not_25_out, not_26_out,
       not_27_out, not_28_out, not_29_out, not_30_out, not_31_out, not_32_out, not_33_out, not_34_out,
       not_35_out, not_36_out, not_37_out, not_38_out, not_39_out, not_40_out;

  not not_1 (not_1_out, a);
  not not_2 (not_2_out, b);
  not not_3 (not_3_out, c);
  not not_4 (not_4_out, d);
  not not_5 (not_5_out, e);
  not not_6 (not_6_out, a);
  not not_7 (not_7_out, b);
  not not_8 (not_8_out, c);
  not not_9 (not_9_out, a);
  not not_10 (not_10_out, b);
  not not_11 (not_11_out, d);
  not not_12 (not_12_out, a);
  not not_13 (not_13_out, b);
  not not_14 (not_14_out, e);
  not not_15 (not_15_out, a);
  not not_16 (not_16_out, c);
  not not_17 (not_17_out, d);
  not not_18 (not_18_out, a);
  not not_19 (not_19_out, c);
  not not_20 (not_20_out, e);
  not not_21 (not_21_out, a);
  not not_22 (not_22_out, d);
  not not_23 (not_23_out, e);
  not not_24 (not_24_out, a);
  not not_25 (not_25_out, b);
  not not_26 (not_26_out, c);
  not not_27 (not_27_out, d);
  not not_28 (not_28_out, b);
  not not_29 (not_29_out, c);
  not not_30 (not_30_out, e);
  not not_31 (not_31_out, b);
  not not_32 (not_32_out, d);
  not not_33 (not_33_out, e);
  not not_34 (not_34_out, b);
  not not_35 (not_35_out, c);
  not not_36 (not_36_out, d);
  not not_37 (not_37_out, e);
  not not_38 (not_38_out, c);
  not not_39 (not_39_out, d);
  not not_40 (not_40_out, e);
  and and_1 (and_1_out, not_1_out, not_2_out, not_3_out, not_4_out, not_5_out);
  and and_2 (and_2_out, not_6_out, not_7_out, not_8_out, d, e);
  and and_3 (and_3_out, not_9_out, not_10_out, c, not_11_out, e);
  and and_4 (and_4_out, not_12_out, not_13_out, c, d, not_14_out);
  and and_5 (and_5_out, not_15_out, b, not_16_out, not_17_out, e);
  and and_6 (and_6_out, not_18_out, b, not_19_out, d, not_20_out);
  and and_7 (and_7_out, not_21_out, b, c, not_22_out, not_23_out);
  and and_8 (and_8_out, not_24_out, b, c, d, e);
  and and_9 (and_9_out, a, not_25_out, not_26_out, not_27_out, e);
  and and_10 (and_10_out, a, not_28_out, not_29_out, d, not_30_out);
  and and_11 (and_11_out, a, not_31_out, c, not_32_out, not_33_out);
  and and_12 (and_12_out, a, not_34_out, c, d, e);
  and and_13 (and_13_out, a, b, not_35_out, not_36_out, not_37_out);
  and and_14 (and_14_out, a, b, not_38_out, d, e);
  and and_15 (and_15_out, a, b, c, not_39_out, e);
  and and_16 (and_16_out, a, b, c, d, not_40_out);
  or or_1 (x, and_1_out, and_2_out, and_3_out, and_4_out, and_5_out, and_6_out, and_7_out, and_8_out, and_9_out, and_10_out, and_11_out, and_12_out, and_13_out, and_14_out, and_15_out, and_16_out);

  // Notes on the sheet:
  //   3.4.2: Verifying the basic XNOR gate(upto 5 inputs) for all input combinations.(Using circuit analysis)
endmodule
