// Logisim project Lab-Final_P-01.circ as structural Verilog: 2 circuits, main circuit main
module main (
  input  MSB,
  input  B,
  input  C,
  input  LSB,
  output F
);

  wire m1_out, m2_out, m3_out, m6_out, m9_out, m11_out, not_1_out, not_2_out, not_3_out, not_4_out;

  not not_1 (not_1_out, MSB);
  not not_2 (not_2_out, B);
  not not_3 (not_3_out, C);
  not not_4 (not_4_out, LSB);
  and m1 (m1_out, not_1_out, not_2_out, not_3_out, LSB);
  and m2 (m2_out, not_1_out, not_2_out, C, not_4_out);
  and m3 (m3_out, not_1_out, not_2_out, C, LSB);
  and m6 (m6_out, not_1_out, B, C, not_4_out);
  and m9 (m9_out, MSB, not_2_out, not_3_out, LSB);
  and m11 (m11_out, MSB, not_2_out, C, LSB);
  or or_1 (F, m1_out, m2_out, m3_out, m6_out, m9_out, m11_out);

  // Notes on the sheet:
  //   A
  //   D
  //   1. F(A, B, C, D) = SOP(1,2,3,6,9,11)
  //   (Using Drag and Drop)
endmodule

module Analyze_Circuit (
  input  A,
  input  B,
  input  C,
  input  D,
  output F
);

  wire and_1_out, and_2_out, not_1_out, not_2_out, not_3_out;

  not not_1 (not_1_out, B);
  not not_2 (not_2_out, A);
  not not_3 (not_3_out, D);
  and and_1 (and_1_out, not_1_out, D);
  and and_2 (and_2_out, not_2_out, C, not_3_out);
  or or_1 (F, and_1_out, and_2_out);

  // Notes on the sheet:
  //   MSB
  //   LSB
  //   1. F(A, B, C, D) = SOP(1,2,3,6,9,11)(Using Analyze Circuit)
endmodule
