// Logisim project Lab-Final_P-02.circ as structural Verilog: 1 circuit, main circuit main
module main (
  input  MSB,
  input  B,
  input  C,
  input  D,
  output F
);

  wire and_1_out, and_2_out, not_1_out, not_2_out, not_3_out;

  not not_1 (not_1_out, MSB);
  not not_2 (not_2_out, B);
  not not_3 (not_3_out, D);
  and and_1 (and_1_out, not_1_out, C, not_3_out);
  and and_2 (and_2_out, not_2_out, D);
  or or_1 (F, and_1_out, and_2_out);

  // Notes on the sheet:
  //   A
  //   LSB
  //   2. Simplified Version of F
endmodule
