// Logisim project Lab-Final_P-03.circ as structural Verilog: 1 circuit, main circuit main
module main (
  input  ENABLE,
  output MSB,
  output out_3,
  output LSB
);

  wire and_1_out, and_2_out, and_3_out, clock_1_out, d_ff_1_qn, d_ff_2_qn, t_ff_1_qn;

  and and_1 (and_1_out, d_ff_2_qn, d_ff_1_qn);
  Clock clock_1 (.out(clock_1_out));
  D_Flip_Flop d_ff_1 (.clk(clock_1_out), .D(and_1_out), .Q(LSB), .Qn(d_ff_1_qn), .en(ENABLE));  // open: preset, reset
  and and_2 (and_2_out, d_ff_2_qn, d_ff_1_qn);
  T_Flip_Flop t_ff_1 (.clk(clock_1_out), .T(and_2_out), .Q(out_3), .Qn(t_ff_1_qn), .en(ENABLE));  // open: preset, reset
  and and_3 (and_3_out, LSB, t_ff_1_qn);
  D_Flip_Flop d_ff_2 (.clk(clock_1_out), .D(and_3_out), .Q(MSB), .Qn(d_ff_2_qn), .en(ENABLE));  // open: preset, reset

  // Notes on the sheet:
  //   CLOCK
  //   LSB
  //   A
  //   3. Designing a Counter that Counts 0, 3, 2, 1, 4, 0 Using Different Flip-Flops  
  //   B
  //   MSB
  //   C
endmodule
